# Fritzing sketch ESP32Cam_NodeMCU_Update (saved by Fritzing 0.9.3b)

parts:
  U1 = NodeMCU V3.0
  ESP32_-_Back1 = ESP32 - CAM

nets:
  N1: U1.RX, ESP32_-_Back1.GPIO3_/_RX
  N2: U1.TX, ESP32_-_Back1.GPIO1_/_TX
  GND: U1.GND, ESP32_-_Back1.GND
  3V3: U1.3V3, ESP32_-_Back1.3.3V

custom parts:
  NodeMCU V3.0: NodeMcu V3 Lua WIFI Development Board
  ESP32 - CAM: The ESP32-CAM has a very competitive small-size camera module that can operate independently as a minimum system with a footprint of only 27*40.5*4.5mm and a deep sleep current of up to 6mA.
